# Fritzing sketch solar position system (saved by Fritzing 0.9.3b)
breadboards: 1

parts:
  Part1 = Arduino Nano (Rev3.0) (ICSP)
  R1 = PHOTOCELL [package=photocell]
  R2 = PHOTOCELL [package=photocell]
  R3 = PHOTOCELL [package=photocell]
  R4 = PHOTOCELL [package=photocell]
  R5 = Resistor [tolerance=±5% resistance=10k package="1206 [SMD]"]
  R6 = Resistor [tolerance=±5% resistance=10k package="1206 [SMD]"]
  R7 = Resistor [tolerance=±5% resistance=10k package="1206 [SMD]"]
  R8 = Resistor [tolerance=±5% resistance=10k package="1206 [SMD]"]
  R9 = Temperature Sensor (Thermistor) [thermistor_type=NTC package=THT]
  R10 = Resistor [tolerance=±5% resistance=10k package="1206 [SMD]"]
  R11 = Resistor [tolerance=±5% resistance=10k package="1206 [SMD]"]
  R12 = Resistor [tolerance=±5% resistance=10k package="1206 [SMD]"]
  R13 = Resistor [tolerance=±5% resistance=10k package="1206 [SMD]"]
  R14 = Resistor [tolerance=±5% resistance=10k package="1206 [SMD]"]

nets:
  N1: Part1.GND, R5.Pin_0, R6.Pin_0, R7.Pin_0, R8.Pin_0, R10.Pin_0
  N2: Part1.D2, R11.Pin_1
  N3: Part1.D3, R12.Pin_1
  N4: Part1.D4, R13.Pin_1
  N5: Part1.D5, R14.Pin_1
  N6: Part1.5V, R1.P$1, R2.P$1, R3.P$1, R4.P$1, R9.pin_1
  N7: Part1.A4, R9.pin_0, R10.Pin_1
  N8: Part1.A3, R4.P$2, R8.Pin_1
  N9: Part1.A2, R3.P$2, R7.Pin_1
  N10: Part1.A1, R2.P$2, R6.Pin_1
  N11: Part1.A0, R1.P$2, R5.Pin_1
  N12: R11.Pin_0, R12.Pin_0, R13.Pin_0, R14.Pin_0
